# Fritzing sketch detektor warna (saved by Fritzing 0.9.3b)
breadboards: 1

parts:
  R1 = PHOTOCELL [package=photocell-kit]
  R2 = Resistor [tolerance=±5% resistance=220 package="2010 [SMD]"]
  Part1 = Arduino Uno (Rev3)
  R3 = Resistor [tolerance=±5% resistance=10k package=THT]
  R4 = Resistor [tolerance=±5% resistance=10k package=THT]
  LED1 = RGB LED (com. cathode, rgb) [package="5 mm [THT]"]
  S1 = Pushbutton [package=THT]

nets:
  N1: R1.P$1, R2.Pin_0, Part1.5V, R4.Pin_0
  N2: R1.P$2, Part1.A0, R3.Pin_0
  N3: R2.Pin_1, LED1.common_cathode
  N4: Part1.D9_PWM, LED1.blue_anode
  N5: Part1.D10_PWM/SS, LED1.green_anode
  N6: Part1.D11_PWM/MOSI, LED1.red_anode
  N7: Part1.D2, R4.Pin_1, S1.leg1
  N8: Part1.GND, R3.Pin_1, S1.leg0
